# Fritzing sketch running16leds (saved by Fritzing 0.8.3b)
breadboards: 2

parts:
  元件1 = Arduino Uno (Rev3)
  LED1 = LED - 5mm [color="Red (633nm)" package="5 mm [THT]"]
  LED2 = LED - 5mm [color="Red (633nm)" package="5 mm [THT]"]
  LED3 = LED - 5mm [color="Red (633nm)" package="5 mm [THT]"]
  LED4 = LED - 5mm [color="Red (633nm)" package="5 mm [THT]"]
  LED5 = LED - 5mm [color="Red (633nm)" package="5 mm [THT]"]
  LED6 = LED - 5mm [color="Red (633nm)" package="5 mm [THT]"]
  LED7 = LED - 5mm [color="Red (633nm)" package="5 mm [THT]"]
  LED8 = LED - 5mm [color="Red (633nm)" package="5 mm [THT]"]
  LED9 = LED - 5mm [color="Red (633nm)" package="5 mm [THT]"]
  LED10 = LED - 5mm [color="Red (633nm)" package="5 mm [THT]"]
  LED11 = LED - 5mm [color="Red (633nm)" package="5 mm [THT]"]
  LED12 = LED - 5mm [color="Red (633nm)" package="5 mm [THT]"]
  LED13 = LED - 5mm [color="Red (633nm)" package="5 mm [THT]"]
  LED14 = LED - 5mm [color="Red (633nm)" package="5 mm [THT]"]
  LED15 = LED - 5mm [color="Red (633nm)" package="5 mm [THT]"]
  LED16 = LED - 5mm [color="Red (633nm)" package="5 mm [THT]"]
  R1 = Resistor [tolerance=±5% resistance=220 package=THT]
  R2 = Resistor [tolerance=±5% resistance=220 package=THT]
  R3 = Resistor [tolerance=±5% resistance=220 package=THT]
  R4 = Resistor [tolerance=±5% resistance=220 package=THT]
  R5 = Resistor [tolerance=±5% resistance=220 package=THT]
  R6 = Resistor [tolerance=±5% resistance=220 package=THT]
  R7 = Resistor [tolerance=±5% resistance=220 package=THT]
  R8 = Resistor [tolerance=±5% resistance=220 package=THT]
  R9 = Resistor [tolerance=±5% resistance=220 package=THT]
  R10 = Resistor [tolerance=±5% resistance=220 package=THT]
  R11 = Resistor [tolerance=±5% resistance=220 package=THT]
  R12 = Resistor [tolerance=±5% resistance=220 package=THT]
  R13 = Resistor [tolerance=±5% resistance=220 package=THT]
  R14 = Resistor [tolerance=±5% resistance=220 package=THT]
  R15 = Resistor [tolerance=±5% resistance=220 package=THT]
  R16 = Resistor [tolerance=±5% resistance=220 package=THT]
  U1 = 74HC595 [package="DIP16 [THT]"]
  U2 = 74HC595 [package="DIP16 [THT]"]

nets:
  GND: 元件1.GND, LED1.cathode, LED2.cathode, LED3.cathode, LED4.cathode, LED5.cathode, LED6.cathode, LED7.cathode, LED8.cathode, LED9.cathode, LED10.cathode, LED11.cathode, LED12.cathode, LED13.cathode, LED14.cathode, LED15.cathode, LED16.cathode, U1.GND, U1.OE, U2.GND, U2.OE
  N1: 元件1.D2, U1.SH_CP, U2.SH_CP
  N2: 元件1.D3_PWM, U1.ST_CP, U2.ST_CP
  N3: 元件1.D4, U2.DS
  VCC: 元件1.5V, U1.MR, U1.VCC, U2.MR, U2.VCC
  N4: LED1.anode, R1.Pin_1
  N5: LED2.anode, R2.Pin_1
  N6: LED3.anode, R3.Pin_1
  N7: LED4.anode, R4.Pin_1
  N8: LED5.anode, R5.Pin_1
  N9: LED6.anode, R6.Pin_1
  N10: LED7.anode, R7.Pin_1
  N11: LED8.anode, R8.Pin_1
  N12: LED9.anode, R9.Pin_1
  N13: LED10.anode, R10.Pin_1
  N14: LED11.anode, R11.Pin_1
  N15: LED12.anode, R12.Pin_1
  N16: LED13.anode, R13.Pin_1
  N17: LED14.anode, R14.Pin_1
  N18: LED15.anode, R15.Pin_1
  N19: LED16.anode, R16.Pin_1
  N20: R1.Pin_0, U1.Q7
  N21: R2.Pin_0, U1.Q6
  N22: R3.Pin_0, U1.Q5
  N23: R4.Pin_0, U1.Q4
  N24: R5.Pin_0, U1.Q3
  N25: R6.Pin_0, U1.Q2
  N26: R7.Pin_0, U1.Q1
  N27: R8.Pin_0, U1.Q0
  N28: R9.Pin_0, U2.Q7
  N29: R10.Pin_0, U2.Q6
  N30: R11.Pin_0, U2.Q5
  N31: R12.Pin_0, U2.Q4
  N32: R13.Pin_0, U2.Q3
  N33: R14.Pin_0, U2.Q2
  N34: R15.Pin_0, U2.Q1
  N35: R16.Pin_0, U2.Q0
  N36: U1.DS, U2.Q7'
