# Fritzing sketch ch03_led_pwm (saved by Fritzing 0.8.3b)
breadboards: 1

parts:
  LED1 = LED - 5mm [color="Red (633nm)" package="5 mm [THT]"]
  R1 = Resistor [tolerance=±5% resistance=220 package=THT]
  元件1 = Arduino Uno (Rev3)
  R2 = Rotary Potentiometer (Large) [package=THT]

nets:
  N1: LED1.cathode, 元件1.GND, R2.leg2
  N2: LED1.anode, R1.Pin_0
  N3: R1.Pin_1, 元件1.D11_PWM/MOSI
  N4: 元件1.A0, R2.wiper
  N5: 元件1.5V, R2.leg1

notes:
  220 Ω
  11
  A0
