# Fritzing sketch ch03_led_switch (saved by Fritzing 0.8.3b)
breadboards: 1

parts:
  LED1 = LED - 5mm [color="Red (633nm)" package="5 mm [THT]"]
  R1 = Resistor [tolerance=±5% resistance=220 package=THT]
  元件1 = Arduino Uno (Rev3)
  R2 = Resistor [tolerance=±5% resistance=10k package=THT]
  S1 = Pushbutton [package="[THT]"]

nets:
  N1: LED1.cathode, 元件1.GND, R2.Pin_0
  N2: LED1.anode, R1.Pin_0
  N3: R1.Pin_1, 元件1.D11_PWM/MOSI
  N4: 元件1.D7, R2.Pin_1, S1.Pin_3, S1.Pin_4
  N5: 元件1.5V, S1.Pin_1, S1.Pin_2

notes:
  220 Ω
  10k Ω
  GND
  5V
  11
  7
