# Fritzing sketch ch03_repeat_after_me (saved by Fritzing 0.8.3b)
breadboards: 1

parts:
  元件1 = Arduino Uno (Rev3)
  LED1 = LED - 5mm [color="Red (633nm)" package="5 mm [THT]"]
  R1 = Resistor [tolerance=±5% resistance=220 package=THT]
  S1 = Pushbutton [package="[THT]"]
  LED2 = LED - 5mm [color="Red (633nm)" package="5 mm [THT]"]
  R2 = Resistor [tolerance=±5% resistance=220 package=THT]
  S2 = Pushbutton [package="[THT]"]
  LED3 = LED - 5mm [color="Red (633nm)" package="5 mm [THT]"]
  R3 = Resistor [tolerance=±5% resistance=220 package=THT]
  S3 = Pushbutton [package="[THT]"]
  LED4 = LED - 5mm [color="Red (633nm)" package="5 mm [THT]"]
  R4 = Resistor [tolerance=±5% resistance=220 package=THT]
  S4 = Pushbutton [package="[THT]"]
  LED5 = LED - 5mm [color="Red (633nm)" package="5 mm [THT]"]
  R5 = Resistor [tolerance=±5% resistance=220 package=THT]
  S5 = Pushbutton [package="[THT]"]

nets:
  N1: 元件1.ICSP_MISO, 元件1.D12/MISO, R1.Pin_1
  N2: 元件1.GND, LED1.cathode, S1.Pin_3, S1.Pin_4, LED2.cathode, S2.Pin_3, S2.Pin_4, LED3.cathode, S3.Pin_3, S3.Pin_4, LED4.cathode, S4.Pin_3, S4.Pin_4, LED5.cathode, S5.Pin_3, S5.Pin_4
  N3: 元件1.D8, R3.Pin_1
  N4: 元件1.D9_PWM, S2.Pin_1, S2.Pin_2
  N5: 元件1.D10_PWM/SS, R2.Pin_1
  N6: 元件1.D11_PWM/MOSI, S1.Pin_1, S1.Pin_2
  N7: 元件1.D3_PWM, S5.Pin_1, S5.Pin_2
  N8: 元件1.D4, R5.Pin_1
  N9: 元件1.D5_PWM, S4.Pin_1, S4.Pin_2
  N10: 元件1.D6_PWM, R4.Pin_1
  N11: 元件1.D7, S3.Pin_1, S3.Pin_2
  N12: LED1.anode, R1.Pin_0
  N13: LED2.anode, R2.Pin_0
  N14: LED3.anode, R3.Pin_0
  N15: LED4.anode, R4.Pin_0
  N16: LED5.anode, R5.Pin_0
