# Fritzing sketch ch04_drum (saved by Fritzing 0.8.3b)
breadboards: 1

parts:
  元件1 = Arduino Uno (Rev3)
  U1 = LCD-16X2 [package=lcd-16x2]
  R1 = Rotary Potentiometer (Large) [package=THT]
  J1 = Basic Force Sensing Resistor (FSR) [package=THT]
  R2 = Resistor [tolerance=±5% resistance=10k package=THT]
  J2 = Piezo Speaker

nets:
  N1: 元件1.A0, J1.pin_1, R2.Pin_0
  GND: 元件1.GND, U1.VSS, U1.R_W, U1.K, R1.leg1, R2.Pin_1, J2.pin1
  N2: 元件1.D9_PWM, J2.pin2
  N3: 元件1.D2, U1.RS
  N4: 元件1.D3_PWM, U1.E
  N5: 元件1.D4, U1.DB4
  N6: 元件1.D5_PWM, U1.DB5
  N7: 元件1.D6_PWM, U1.DB6
  N8: 元件1.D7, U1.DB7
  5V: 元件1.5V, U1.VDD, U1.A, R1.leg2, J1.pin_0
  N9: U1.VO, R1.wiper
