# Fritzing sketch ch04_photoresistor (saved by Fritzing 0.8.3b)
breadboards: 1

parts:
  R1 = Resistor [tolerance=±5% resistance=10k package=THT]
  元件1 = Arduino Uno (Rev3)
  R2 = PHOTOCELL [package=photocell-kit]
  LED1 = LED - 5mm [color="Red (633nm)" package="5 mm [THT]"]
  R3 = Resistor [tolerance=±5% resistance=220 package=THT]

nets:
  N1: R1.Pin_0, 元件1.A0, R2.P$2
  N2: R1.Pin_1, 元件1.GND, LED1.cathode
  N3: 元件1.ICSP_MOSI, 元件1.D11_PWM/MOSI, R3.Pin_0
  N4: 元件1.5V, R2.P$1
  N5: LED1.anode, R3.Pin_1

notes:
  10kΩ
  220Ω
  11
  A0
