# Fritzing sketch ch04_voltage_divider (saved by Fritzing 0.8.3b)
breadboards: 1

parts:
  R1 = Resistor [tolerance=±5% resistance=10k package=THT]
  R2 = Resistor [tolerance=±5% resistance=10k package=THT]
  元件1 = Arduino Uno (Rev3)

nets:
  N1: R1.Pin_0, 元件1.5V
  N2: R1.Pin_1, R2.Pin_0, 元件1.A0
  N3: R2.Pin_1, 元件1.GND

notes:
  R1
  R2
  5V
  GND
  A0
