# Fritzing sketch ch05_7segled (saved by Fritzing 0.8.3b)
breadboards: 1

parts:
  DI1 = 7-Segment LED Display [package=THT]
  R1 = Resistor [tolerance=±5% resistance=220 package=THT]
  R2 = Resistor [tolerance=±5% resistance=220 package=THT]
  R3 = Resistor [tolerance=±5% resistance=220 package=THT]
  R4 = Resistor [tolerance=±5% resistance=220 package=THT]
  R5 = Resistor [tolerance=±5% resistance=220 package=THT]
  R6 = Resistor [tolerance=±5% resistance=220 package=THT]
  R7 = Resistor [tolerance=±5% resistance=220 package=THT]
  R8 = Resistor [tolerance=±5% resistance=220 package=THT]
  元件1 = Arduino Uno (Rev3)

nets:
  N1: DI1.cathodeE, R6.Pin_1
  N2: DI1.cathodeD, R5.Pin_1
  N3: DI1.commAnode, 元件1.GND
  N4: DI1.cathodeC, R7.Pin_0
  N5: DI1.cathodeDP, R8.Pin_0
  N6: DI1.cathodeB, R4.Pin_0
  N7: DI1.cathodeA, R3.Pin_0
  N8: DI1.cathodeF, R1.Pin_1
  N9: DI1.cathodeG, R2.Pin_1
  N10: R1.Pin_0, 元件1.D9_PWM
  N11: R2.Pin_0, 元件1.D8
  N12: R3.Pin_1, 元件1.D2
  N13: R4.Pin_1, 元件1.D3_PWM
  N14: R5.Pin_0, 元件1.D6_PWM
  N15: R6.Pin_0, 元件1.D7
  N16: R7.Pin_1, 元件1.D5_PWM
  N17: R8.Pin_1, 元件1.D4

notes:
  5V
  GND
