# Fritzing sketch ch05_7segled_decoder_2 (saved by Fritzing 0.8.3b)
breadboards: 2

parts:
  DI1 = 7-Segment LED Display [package=THT]
  R1 = Resistor [tolerance=±5% resistance=220 package=THT]
  R2 = Resistor [tolerance=±5% resistance=220 package=THT]
  R3 = Resistor [tolerance=±5% resistance=220 package=THT]
  R4 = Resistor [tolerance=±5% resistance=220 package=THT]
  R5 = Resistor [tolerance=±5% resistance=220 package=THT]
  R6 = Resistor [tolerance=±5% resistance=220 package=THT]
  R7 = Resistor [tolerance=±5% resistance=220 package=THT]
  元件1 = Arduino Uno (Rev3)
  IC1 = IC, DIP package, 16 pins [chip_label=4511]

nets:
  N1: DI1.cathodeE, R6.Pin_1
  N2: DI1.cathodeD, R5.Pin_1
  N3: DI1.commAnode, DI1.cathodeDP, 元件1.GND
  N4: DI1.cathodeC, R7.Pin_0
  N5: DI1.cathodeB, R4.Pin_0
  N6: DI1.cathodeA, R3.Pin_0
  N7: DI1.cathodeF, R1.Pin_1
  N8: DI1.cathodeG, R2.Pin_1
  N9: 元件1.D4, IC1.pin2
  N10: 元件1.D5_PWM, IC1.pin1
  N11: 元件1.5V, IC1.pin3, IC1.pin4

notes:
  5V
  GND
