# Fritzing sketch ch05_clock_rtc (saved by Fritzing 0.8.3b)
breadboards: 1

parts:
  元件1 = Arduino Uno (Rev3)
  IC2 = DS1307 [package=THT]
  C1 = Capacitor [package=cap-pth-small2]
  R2 = 2.2k Ω Resistor [package=THT]
  R3 = 2.2k Ω Resistor [package=THT]
  XTAL2 = CRYSTAL - kHz [frequency="32 kHz"]
  BAT1 = Battery Holders [package=battcom_20mm_pth]

nets:
  N1: 元件1.A4/SDA, IC2.SDA_-_I2C_Data, R3.Pin_0
  N2: 元件1.A5/SCL, IC2.SCL_-_I2C_Clock, R2.Pin_0
  N3: 元件1.GND, IC2.0V, C1.1, BAT1.-
  N4: 元件1.5V, IC2.+V, C1.2, R2.Pin_1, R3.Pin_1
  N5: IC2.X1_-_Crystal, XTAL2.pin_1
  N6: IC2.X2_-_Crystal, XTAL2.pin_0
  N7: IC2.Vbat_-_Backup_Supply, BAT1.+
