# Fritzing sketch ch05_lcd (saved by Fritzing 0.8.3b)
breadboards: 1

parts:
  元件1 = Arduino Uno (Rev3)
  U1 = LCD-16X2 [package=lcd-16x2]
  R1 = Rotary Potentiometer (Large) [package=THT]
  S1 = Pushbutton [package="[THT]"]

nets:
  GND: 元件1.GND, U1.VSS, U1.R_W, U1.K, R1.leg1, S1.Pin_3, S1.Pin_4
  N1: 元件1.D12/MISO, S1.Pin_1, S1.Pin_2
  N2: 元件1.D2, U1.RS
  N3: 元件1.D3_PWM, U1.E
  N4: 元件1.D4, U1.DB4
  N5: 元件1.D5_PWM, U1.DB5
  N6: 元件1.D6_PWM, U1.DB6
  N7: 元件1.D7, U1.DB7
  5V: 元件1.5V, U1.VDD, U1.A, R1.leg2
  N8: U1.VO, R1.wiper

notes:
  5V
  GND
  12
