# Fritzing sketch ch05_ledmatrix_uno_a (saved by Fritzing 0.8.3b)
breadboards: 1

parts:
  U1 = MAX7219 [package=dil24]
  8x8_LED_Matrix1 = 8x8 LED Matrix 1388ASR  # not connected
  元件1 = Arduino Uno (Rev3)
  R1 = Resistor [tolerance=±5% resistance=22k package=THT]

nets:
  N1: U1.DIN, 元件1.ICSP_MOSI, 元件1.D11_PWM/MOSI
  GND: U1.GND, U1.GND2, 元件1.GND
  N2: U1.LOAD, 元件1.D10_PWM/SS
  N3: U1.CLK, 元件1.ICSP_SCK, 元件1.D13/SCK
  N4: U1.ISET, R1.Pin_1
  VCC: U1.VCC, 元件1.5V, R1.Pin_0

custom parts:
  8x8 LED Matrix 1388ASR: Red Color Common Anode 8x8 LED Matrix
