# Fritzing sketch ch05_ledmatrix_uno_b (saved by Fritzing 0.8.3b)
breadboards: 1

parts:
  U1 = MAX7219 [package=dil24]
  8x8_LED_Matrix1 = 8x8 LED Matrix 1388ASR
  R1 = Resistor [tolerance=±5% resistance=22k package=THT]

nets:
  N1: U1.DIG0, 8x8_LED_Matrix1.Pin_9
  N2: U1.DIG4, 8x8_LED_Matrix1.Pin_1
  GND: U1.GND, U1.GND2
  N3: U1.DIG6, 8x8_LED_Matrix1.Pin_2
  N4: U1.DIG2, 8x8_LED_Matrix1.Pin_8
  N5: U1.DIG3, 8x8_LED_Matrix1.Pin_12
  N6: U1.DIG7, 8x8_LED_Matrix1.Pin_5
  N7: U1.DIG5, 8x8_LED_Matrix1.Pin_7#7
  N8: U1.DIG1, 8x8_LED_Matrix1.Pin14
  N9: U1.SEGA, 8x8_LED_Matrix1.Pin_3
  N10: U1.SEGF, 8x8_LED_Matrix1.Pin_15
  N11: U1.SEGB, 8x8_LED_Matrix1.Pin_4
  N12: U1.SEGG, 8x8_LED_Matrix1.Pin_16
  N13: U1.ISET, R1.Pin_1
  N14: U1.VCC, R1.Pin_0
  N15: U1.SEGC, 8x8_LED_Matrix1.Pin_7#10
  N16: U1.SEGE, 8x8_LED_Matrix1.Pin_11
  N17: U1.SEGDP, 8x8_LED_Matrix1.Pin_13
  N18: U1.SEGD, 8x8_LED_Matrix1.Pin_6

custom parts:
  8x8 LED Matrix 1388ASR: Red Color Common Anode 8x8 LED Matrix
