# Fritzing sketch ch05_rgbled (saved by Fritzing 0.8.3b)
breadboards: 1

parts:
  R1 = Resistor [tolerance=±5% resistance=220 package=THT]
  LED1 = RGB LED (com. cathode, rgb) [package="5 mm [THT]"]
  R2 = Resistor [tolerance=±5% resistance=220 package=THT]
  R3 = Resistor [tolerance=±5% resistance=220 package=THT]
  元件1 = Arduino Uno (Rev3)

nets:
  N1: R1.Pin_0, 元件1.ICSP_MOSI, 元件1.D11_PWM/MOSI
  N2: R1.Pin_1, LED1.red_anode
  N3: LED1.common_cathode, 元件1.GND
  N4: LED1.green_anode, R2.Pin_1
  N5: LED1.blue_anode, R3.Pin_1
  N6: R2.Pin_0, 元件1.D10_PWM/SS
  N7: R3.Pin_0, 元件1.D9_PWM

notes:
  GND
  5V
  220Ω
