# Fritzing sketch ch05_rgbled_pwm (saved by Fritzing 0.8.3b)
breadboards: 1

parts:
  R1 = Resistor [tolerance=±5% resistance=220 package=THT]
  LED1 = RGB LED (com. cathode, rgb) [package="5 mm [THT]"]
  R2 = Resistor [tolerance=±5% resistance=220 package=THT]
  R3 = Resistor [tolerance=±5% resistance=220 package=THT]
  元件1 = Arduino Uno (Rev3)
  R4 = Rotary Potentiometer (Large) [package=THT]
  R5 = Rotary Potentiometer (Large) [package=THT]
  R6 = Rotary Potentiometer (Large) [package=THT]

nets:
  N1: R1.Pin_0, 元件1.ICSP_MOSI, 元件1.D11_PWM/MOSI
  N2: R1.Pin_1, LED1.red_anode
  N3: LED1.common_cathode, 元件1.GND, R4.leg2, R5.leg2, R6.leg2
  N4: LED1.green_anode, R2.Pin_1
  N5: LED1.blue_anode, R3.Pin_1
  N6: R2.Pin_0, 元件1.D10_PWM/SS
  N7: R3.Pin_0, 元件1.D9_PWM
  N8: 元件1.A0, R4.wiper
  N9: 元件1.A1, R5.wiper
  N10: 元件1.A2, R6.wiper
  N11: 元件1.5V, R4.leg1, R5.leg1, R6.leg1

notes:
  220Ω
  A0
  A1
  A2
