# Fritzing sketch ch06_keyboard (saved by Fritzing 0.8.3b)
breadboards: 1

parts:
  元件1 = Arduino Uno (Rev3)
  J1 = Piezo Speaker
  S1 = Pushbutton [package="[THT]"]
  S2 = Pushbutton [package="[THT]"]
  S3 = Pushbutton [package="[THT]"]
  S4 = Pushbutton [package="[THT]"]
  S5 = Pushbutton [package="[THT]"]
  S6 = Pushbutton [package="[THT]"]
  S7 = Pushbutton [package="[THT]"]
  S8 = Pushbutton [package="[THT]"]
  S9 = Pushbutton [package="[THT]"]

nets:
  N1: 元件1.ICSP_MOSI, 元件1.D11_PWM/MOSI, S2.Pin_1, S2.Pin_2
  N2: 元件1.GND, J1.pin1, S1.Pin_3, S1.Pin_4, S2.Pin_3, S2.Pin_4, S3.Pin_3, S3.Pin_4, S4.Pin_3, S4.Pin_4, S5.Pin_3, S5.Pin_4, S6.Pin_3, S6.Pin_4, S7.Pin_3, S7.Pin_4, S8.Pin_3, S8.Pin_4, S9.Pin_3, S9.Pin_4
  N3: 元件1.D8, S5.Pin_1, S5.Pin_2
  N4: 元件1.D9_PWM, S4.Pin_1, S4.Pin_2
  N5: 元件1.D10_PWM/SS, S3.Pin_1, S3.Pin_2
  N6: 元件1.D12/MISO, S1.Pin_1, S1.Pin_2
  N7: 元件1.D3_PWM, J1.pin2
  N8: 元件1.D4, S9.Pin_1, S9.Pin_2
  N9: 元件1.D5_PWM, S8.Pin_1, S8.Pin_2
  N10: 元件1.D6_PWM, S7.Pin_1, S7.Pin_2
  N11: 元件1.D7, S6.Pin_1, S6.Pin_2

notes:
  5V
  GND
