# Fritzing sketch ch06_microphone (saved by Fritzing 0.8.3b)
breadboards: 1

parts:
  U1 = LM 358 Dual Op-Amp [package="DIP8 [THT]"]
  元件1 = Arduino Uno (Rev3)
  MIC1 = Microphone
  R1 = Resistor [tolerance=±5% resistance=1.5k package=THT]
  C1 = Capacitor [package=cap-pth-small2]
  R2 = Resistor [tolerance=±5% resistance=82k package=THT]
  R3 = Resistor [tolerance=±5% resistance=1k package=THT]
  R4 = Resistor [tolerance=±5% resistance=100k package=THT]

nets:
  N1: U1.connector0, 元件1.A0, R4.Pin_1
  N2: U1.connector1, R3.Pin_0, R4.Pin_0
  N3: U1.connector2, C1.1, R2.Pin_0
  N4: U1.connector3, 元件1.GND, MIC1.pin1, R3.Pin_1
  N5: U1.connector7, 元件1.5V, R1.Pin_0, R2.Pin_1
  N6: MIC1.pin2, R1.Pin_1, C1.2

notes:
  1.5kΩ
  82kΩ
  100kΩ
  1kΩ
  GND
  5V
  A0
