# Fritzing sketch ch06_microphone_blowgame (saved by Fritzing 0.8.3b)
breadboards: 1

parts:
  U1 = LM 358 Dual Op-Amp [package="DIP8 [THT]"]
  元件1 = Arduino Uno (Rev3)
  MIC1 = Microphone
  R1 = Resistor [tolerance=±5% resistance=1.5k package=THT]
  C1 = Capacitor [package=cap-pth-small2]
  R2 = Resistor [tolerance=±5% resistance=82k package=THT]
  R3 = Resistor [tolerance=±5% resistance=1k package=THT]
  R4 = Resistor [tolerance=±5% resistance=100k package=THT]
  U2 = LCD-16X2 [package=lcd-16x2]
  S1 = Pushbutton [package="[THT]"]
  R5 = Rotary Potentiometer (Large) [package=THT]

nets:
  N1: U1.connector0, 元件1.A0, R4.Pin_1
  N2: U1.connector1, R3.Pin_0, R4.Pin_0
  N3: U1.connector2, C1.1, R2.Pin_0
  GND: U1.connector3, 元件1.GND, MIC1.pin1, R3.Pin_1, U2.VSS, U2.R_W, U2.K, S1.Pin_3, S1.Pin_4, R5.leg1
  5V: U1.connector7, 元件1.5V, R1.Pin_0, R2.Pin_1, U2.VDD, U2.A, R5.leg2
  N4: 元件1.D8, S1.Pin_1, S1.Pin_2
  N5: 元件1.D2, U2.RS
  N6: 元件1.D3_PWM, U2.E
  N7: 元件1.D4, U2.DB4
  N8: 元件1.D5_PWM, U2.DB5
  N9: 元件1.D6_PWM, U2.DB6
  N10: 元件1.D7, U2.DB7
  N11: MIC1.pin2, R1.Pin_1, C1.2
  N12: U2.VO, R5.wiper

notes:
  1.5kΩ
  82kΩ
  100kΩ
  1kΩ
  GND
  5V
  A0
