# Fritzing sketch ch06_theremin (saved by Fritzing 0.8.3b)
breadboards: 1

parts:
  元件1 = Arduino Uno (Rev3)
  J1 = Piezo Speaker
  R1 = PHOTOCELL [package=photocell-kit]
  R2 = Resistor [tolerance=±5% resistance=10k package=THT]

nets:
  N1: 元件1.A0, R1.P$2, R2.Pin_0
  N2: 元件1.GND, J1.pin1, R2.Pin_1
  N3: 元件1.D3_PWM, J1.pin2
  N4: 元件1.5V, R1.P$1

notes:
  3
  A0
  GND
  5V
