# Fritzing sketch ch06_twotones (saved by Fritzing 0.8.3b)
breadboards: 1

parts:
  元件1 = Arduino Uno (Rev3)
  J1 = Piezo Speaker
  J2 = Piezo Speaker

nets:
  N1: 元件1.ICSP_MOSI, 元件1.D11_PWM/MOSI, J2.pin2
  N2: 元件1.GND, J1.pin1, J2.pin1
