# Fritzing sketch ch07_BMP085 (saved by Fritzing 0.8.3b)
breadboards: 1

parts:
  元件1 = Arduino Uno (Rev3)
  U1 = LCD-16X2 [package=lcd-16x2]
  R1 = Rotary Potentiometer (Large) [package=THT]
  S2 = Pushbutton [package="[THT]"]
  S3 = Pushbutton [package="[THT]"]
  BMP1 = BMP085 Breakout

nets:
  N1: 元件1.A4/SDA, BMP1.SDA, BMP1.XCLR
  N2: 元件1.A5/SCL, BMP1.SCL
  GND: 元件1.GND, U1.VSS, U1.R_W, U1.K, R1.leg1, S2.Pin_3, S2.Pin_4, S3.Pin_3, S3.Pin_4, BMP1.GND
  N3: 元件1.D8, S3.Pin_1, S3.Pin_2
  N4: 元件1.D9_PWM, S2.Pin_1, S2.Pin_2
  N5: 元件1.D2, U1.RS
  N6: 元件1.D3_PWM, U1.E
  N7: 元件1.D4, U1.DB4
  N8: 元件1.D5_PWM, U1.DB5
  N9: 元件1.D6_PWM, U1.DB6
  N10: 元件1.D7, U1.DB7
  3V3: 元件1.3V3, BMP1.VIN
  5V: 元件1.5V, U1.VDD, U1.A, R1.leg2
  N11: U1.VO, R1.wiper

notes:
  GND
  5V
  SCL
  SDA

custom parts:
  BMP085 Breakout: A breakout for the BMP085 barometric pressure and temperature sensor
