# Fritzing sketch ch07_DHT11 (saved by Fritzing 0.8.3b)
breadboards: 1

parts:
  元件1 = Arduino Uno (Rev3)
  U1 = LCD-16X2 [package=lcd-16x2]
  R1 = Rotary Potentiometer (Large) [package=THT]
  J1 = Piezo Speaker
  DHT1 = DHT11 Humitidy and Temperature Sensor
  R2 = Resistor [tolerance=±5% resistance=10k package=THT]
  S1 = Pushbutton [package="[THT]"]
  S2 = Pushbutton [package="[THT]"]
  S3 = Pushbutton [package="[THT]"]

nets:
  GND: 元件1.GND, U1.VSS, U1.R_W, U1.K, R1.leg1, J1.pin1, DHT1.GND, S1.Pin_3, S1.Pin_4, S2.Pin_3, S2.Pin_4, S3.Pin_3, S3.Pin_4
  N1: 元件1.D8, S3.Pin_1, S3.Pin_2
  N2: 元件1.D9_PWM, S2.Pin_1, S2.Pin_2
  N3: 元件1.D10_PWM/SS, S1.Pin_1, S1.Pin_2
  N4: 元件1.D11_PWM/MOSI, J1.pin2
  N5: 元件1.D12/MISO, DHT1.DATA, R2.Pin_1
  N6: 元件1.D2, U1.RS
  N7: 元件1.D3_PWM, U1.E
  N8: 元件1.D4, U1.DB4
  N9: 元件1.D5_PWM, U1.DB5
  N10: 元件1.D6_PWM, U1.DB6
  N11: 元件1.D7, U1.DB7
  VDD: 元件1.5V, U1.VDD, U1.A, R1.leg2, DHT1.VDD, R2.Pin_0
  N12: U1.VO, R1.wiper

notes:
  GND
  12
  11
  5V
  10kΩ

custom parts:
  DHT11 Humitidy and Temperature Sensor: DHT11 Humidity and Temperature Sensor
