# Fritzing sketch ch08_ir_emitter (saved by Fritzing 0.8.3b)
breadboards: 1

parts:
  元件1 = Arduino Uno (Rev3)
  LED1 = LED - 5mm [color="Infrared (940nm)" package="5 mm [THT]"]
  R1 = Resistor [tolerance=±5% resistance=100 package=THT]

nets:
  N1: 元件1.GND, LED1.cathode
  N2: 元件1.D3_PWM, R1.Pin_1
  N3: LED1.anode, R1.Pin_0

notes:
  GND
  3
  100Ω
