# Fritzing sketch ch08_ir_pair (saved by Fritzing 0.8.3b)
breadboards: 1

parts:
  元件1 = Arduino Uno (Rev3)
  元件2 = Arduino Leonardo (Rev3b)
  IR1 = TSOP312.., 314.. [package=THT]
  IR2 = TSOP312.., 314.. [package=THT]
  LED1 = LED - 5mm [color="Infrared (940nm)" package="5 mm [THT]"]
  R1 = Resistor [tolerance=±5% resistance=100 package=THT]
  LED2 = LED - 5mm [color="Infrared (940nm)" package="5 mm [THT]"]
  R2 = Resistor [tolerance=±5% resistance=100 package=THT]

nets:
  N1: 元件1.GND, IR2.Vs, LED1.cathode
  N2: 元件1.D2, IR2.GND
  N3: 元件1.D3_PWM, R1.Pin_1
  N4: 元件1.5V, IR2.Data
  N5: 元件2.D2/SDA, IR1.GND
  N6: 元件2.5V, IR1.Data
  N7: 元件2.GND, IR1.Vs, LED2.cathode
  N8: 元件2.D13_PWM, R2.Pin_0
  N9: LED1.anode, R1.Pin_0
  N10: LED2.anode, R2.Pin_1

notes:
  5V
  GND
  100Ω
  2
  3
  13
