# Fritzing sketch ch08_ir_piano (saved by Fritzing 0.8.3b)
breadboards: 1

parts:
  元件1 = Arduino Uno (Rev3)
  IR1 = TSOP312.., 314.. [package=THT]
  J1 = Piezo Speaker

nets:
  N1: 元件1.GND, IR1.Vs, J1.pin1
  N2: 元件1.D9_PWM, IR1.GND
  N3: 元件1.5V, IR1.Data

notes:
  GND
  5V
  9
  3
