# Fritzing sketch ch08_ir_receiver (saved by Fritzing 0.8.3b)
breadboards: 1

parts:
  元件1 = Arduino Uno (Rev3)
  IR1 = TSOP312.., 314.. [package=THT]

nets:
  N1: 元件1.GND, IR1.Vs
  N2: 元件1.D2, IR1.GND
  N3: 元件1.5V, IR1.Data

notes:
  2
  GND
  5V
