# Fritzing sketch ch08_pir (saved by Fritzing 0.8.3b)
breadboards: 1

parts:
  PIR1 = PIR sensor
  元件1 = Arduino Uno (Rev3)
  R2 = PHOTOCELL [package=photocell]
  R3 = Resistor [tolerance=±5% resistance=10k package=THT]

nets:
  VDD: PIR1.VDD, 元件1.5V, R2.P$1
  N1: PIR1.SIG, 元件1.D2
  GND: PIR1.GND, 元件1.GND, R3.Pin_1
  N2: 元件1.A0, R2.P$2, R3.Pin_0

notes:
  5V
  GND
  2
  A0
  10kΩ
