# Fritzing sketch ch08_security (saved by Fritzing 0.8.3b)
breadboards: 1

parts:
  元件1 = Arduino Uno (Rev3)
  KEYPAD1 = Membrane Matrix Keypad
  PIR1 = PIR sensor
  J1 = Piezo Speaker
  U1 = LCD-16X2 [package=lcd-16x2]
  R1 = Rotary Potentiometer (Large) [package=THT]

nets:
  N1: 元件1.A0, U1.RS
  N2: 元件1.A1, U1.E
  N3: 元件1.A2, U1.DB4
  N4: 元件1.A3, U1.DB5
  N5: 元件1.A4/SDA, U1.DB6
  N6: 元件1.A5/SCL, U1.DB7
  GND: 元件1.GND, PIR1.GND, J1.pin1, U1.VSS, U1.R_W, U1.K, R1.leg1
  N7: 元件1.D8, KEYPAD1.5
  N8: 元件1.D9_PWM, KEYPAD1.4
  N9: 元件1.D10_PWM/SS, KEYPAD1.3
  N10: 元件1.D11_PWM/MOSI, KEYPAD1.2
  N11: 元件1.D12/MISO, KEYPAD1.1
  N12: 元件1.D2, PIR1.SIG
  N13: 元件1.D3_PWM, J1.pin2
  N14: 元件1.D6_PWM, KEYPAD1.7
  N15: 元件1.D7, KEYPAD1.6
  VDD: 元件1.5V, PIR1.VDD, U1.VDD, U1.A, R1.leg2
  N16: U1.VO, R1.wiper

notes:
  2
  3
  6
  12
  5V
  GND

custom parts:
  Membrane Matrix Keypad: Membrane Matrix 3x4 Keypad
