# Fritzing sketch ch09_7805 (saved by Fritzing 0.8.3b)
breadboards: 1

parts:
  U2 = Voltage Regulator - 5V [package="TO220 [THT]"]
  C1 = Electrolytic Capacitor [capacitance=0.33µF voltage=50V package="100 mil [THT, electrolytic]"]
  C2 = Capacitor [package=cap-pth-small2]

nets:
  N1: U2.input_voltage, C1.+
  N2: U2.GND, C1.-, C2.1
  N3: U2.output_voltage, C2.2

notes:
  0.1μF
  0.33μF
  7805
  5V
  GND
  ＋
  －
