# Fritzing sketch ch09_LD1117V33 (saved by Fritzing 0.8.3b)
breadboards: 1

parts:
  U4 = Voltage Regulator [package=to220-igo]
  C3 = Electrolytic Capacitor [capacitance=10µF voltage=20V package="100 mil [THT, electrolytic]"]
  C4 = Capacitor [package=cap-pth-small2]

nets:
  N1: U4.GND, C3.-, C4.2
  N2: U4.IN, C3.+
  N3: U4.OUT, C4.1

notes:
  10μF
  LD1117V33
  －
  ＋
  GND
  3.3V
  0.1μF
