# Fritzing sketch ch09_LM317 (saved by Fritzing 0.8.3b)
breadboards: 1

parts:
  C3 = Electrolytic Capacitor [capacitance=1µF voltage=20V package="100 mil [THT, electrolytic]"]
  C4 = Capacitor [package=cap-pth-small2]
  R1 = Resistor [tolerance=±5% resistance=240 package=THT]
  R2 = Rotary Potentiometer (Large) [package=THT]
  U5 = Voltage Regulator [package=to220-adj]

nets:
  N1: C3.-, C4.2, R2.wiper
  N2: C3.+, R1.Pin_0, U5.IN
  N3: C4.1, U5.OUT
  N4: R1.Pin_1, R2.leg1, U5.ADJ

notes:
  1μF
  LM317
  Output: －
  0.1μF
  R2:5kΩ
  R1:240Ω
  ＋
  －
  Output: ＋
