# Fritzing sketch ch09_darlington_array (saved by Fritzing 0.8.3b)
breadboards: 1

parts:
  元件1 = Arduino Uno (Rev3)
  R1 = Resistor [tolerance=±5% resistance=68 package=THT]
  LED1 = LED - 5mm [color="Red (633nm)" package="5 mm [THT]"]
  JACK1 = 2.1mm Barrel Jack with Terminal Block
  VCC1 = Battery block 9V
  IC1 = ULN2003A [package="DIP16 [THT]"]
  BATT1 = 4xAA Switchable Battery Pack w/Bare Wire
  LED2 = LED - 5mm [color="Red (633nm)" package="5 mm [THT]"]
  LED3 = LED - 5mm [color="Red (633nm)" package="5 mm [THT]"]
  J1 = Piezo Speaker
  U1 = POT [package=pot_alpha_rv16af-20]

nets:
  N1: 元件1.GND, IC1.0V, BATT1.NEG, U1.A
  N2: 元件1.D3_PWM, IC1.In_1
  N3: 元件1.D4, IC1.In_2
  N4: 元件1.D5_PWM, IC1.In_3
  N5: 元件1.D6_PWM, IC1.In_4
  N6: R1.Pin_0, IC1.COM_-_Common, BATT1.POS, J1.pin2, U1.E
  N7: R1.Pin_1, LED1.cathode
  N8: LED1.anode, LED2.cathode
  N9: JACK1.POS, VCC1.+
  N10: JACK1.NEG, VCC1.-
  N11: IC1.Out_2, J1.pin1
  N12: IC1.Out_1, LED3.anode
  N13: LED2.anode, LED3.cathode

notes:
  68Ω
  ＋
  －

custom parts:
  4xAA Switchable Battery Pack w/Bare Wire: 4xAA Switchable Battery Pack with Bare Wire connection
