# Fritzing sketch ch09_dcmotor (saved by Fritzing 0.9.2b)
breadboards: 1

parts:
  元件1 = Arduino Uno (Rev3)
  R2 = Resistor [tolerance=±5% resistance=1.5k package=THT]
  JACK1 = 2.1mm Barrel Jack with Terminal Block
  VCC1 = Battery block 9V
  VCC2 = Battery
  M1 = DC Motor
  Q1 = TIP120 Hi-Current Darlington Transistor
  C1 = Capacitor [package=cap-pth-small2]
  D1 = Diode [package=diode-1n4001]

nets:
  N1: 元件1.GND, VCC2.-, Q1.EMITTER
  N2: 元件1.D3_PWM, R2.Pin_0
  N3: R2.Pin_1, Q1.BASE
  N4: JACK1.POS, VCC1.+
  N5: JACK1.NEG, VCC1.-
  N6: VCC2.+, M1.pin_2, C1.2, D1.A
  N7: M1.pin_1, Q1.COLLECTOR, C1.1

notes:
  0.1μF
  1.5kΩ
  ＋
  －
  GND
  3
