# Fritzing sketch ch09_transistor_led (saved by Fritzing 0.8.3b)
breadboards: 1

parts:
  元件1 = Arduino Uno (Rev3)
  R1 = Resistor [tolerance=±5% resistance=220 package=THT]
  Q1 = NPN-Transistor [package="TO92 [THT]"]
  R2 = Resistor [tolerance=±5% resistance=15k package=THT]
  LED1 = LED - 5mm [color="Red (633nm)" package="5 mm [THT]"]
  JACK1 = 2.1mm Barrel Jack with Terminal Block
  VCC1 = Battery block 9V

nets:
  N1: 元件1.GND, Q1.E
  N2: 元件1.D2, R2.Pin_1
  N3: 元件1.5V, R1.Pin_1
  N4: R1.Pin_0, LED1.anode
  N5: Q1.B, R2.Pin_0
  N6: Q1.C, LED1.cathode
  N7: JACK1.POS, VCC1.+
  N8: JACK1.NEG, VCC1.-

notes:
  220Ω
  15kΩ
  ＋
  －
  2
  GND
  5V
