# Fritzing sketch ch09_transistor_ledx4 (saved by Fritzing 0.8.3b)
breadboards: 1

parts:
  元件1 = Arduino Uno (Rev3)
  R1 = Resistor [tolerance=±5% resistance=100 package=THT]
  Q1 = NPN-Transistor [package="TO92 [THT]"]
  R2 = Resistor [tolerance=±5% resistance=3.3k package=THT]
  LED1 = LED - 5mm [color="Red (633nm)" package="5 mm [THT]"]
  JACK1 = 2.1mm Barrel Jack with Terminal Block
  VCC1 = Battery block 9V
  VCC2 = Battery
  LED2 = LED - 5mm [color="Red (633nm)" package="5 mm [THT]"]
  LED3 = LED - 5mm [color="Red (633nm)" package="5 mm [THT]"]
  LED4 = LED - 5mm [color="Red (633nm)" package="5 mm [THT]"]

nets:
  N1: 元件1.GND, Q1.E, VCC2.-
  N2: 元件1.D2, R2.Pin_1
  N3: R1.Pin_0, LED1.anode, LED2.anode, LED3.anode, LED4.anode
  N4: R1.Pin_1, VCC2.+
  N5: Q1.B, R2.Pin_0
  N6: Q1.C, LED1.cathode, LED2.cathode, LED3.cathode, LED4.cathode
  N7: JACK1.POS, VCC1.+
  N8: JACK1.NEG, VCC1.-

notes:
  100Ω
  3.3kΩ
  ＋
  －
  GND
  2
