# Fritzing sketch ch10_car_L293D (saved by Fritzing 0.8.3b)
breadboards: 1

parts:
  元件1 = Arduino Uno (Rev3)
  IC1 = L293D [package=THT]
  M1 = DC Motor
  M2 = DC Motor
  JACK1 = 2.1mm Barrel Jack with Terminal Block
  BAT1 = BC9VPC [package=bc9vpc]

nets:
  N1: 元件1.GND, IC1.0V
  N2: 元件1.D8, IC1.In_3
  N3: 元件1.D9_PWM, IC1.Enable_2
  N4: 元件1.D10_PWM/SS, IC1.Enable_1
  N5: 元件1.D11_PWM/MOSI, IC1.In_1
  N6: 元件1.D12/MISO, IC1.In_2
  N7: 元件1.D7, IC1.In_4
  N8: 元件1.5V, IC1.+V
  N9: IC1.Out_1_(_Controlled_by_Enable_1_), M2.pin_1
  N10: IC1.Out_2_(_Controlled_by_Enable_1_), M2.pin_2
  N11: IC1.Out_3_(_Controlled_by_Enable_2_), M1.pin_1
  N12: IC1.Out_4_(_Controlled_by_Enable_2_), M1.pin_2
  N13: JACK1.POS, BAT1.V-
  N14: JACK1.NEG, BAT1.V+

notes:
  ＋
  －
  GND
  5V
  Right
  Left
