# Fritzing sketch ch10_dcmotor_driver (saved by Fritzing 0.8.3b)
breadboards: 1

parts:
  元件1 = Arduino Uno (Rev3)
  IC1 = L293D [package=THT]
  M1 = DC Motor
  R1 = Rotary Potentiometer (Large) [package=THT]

nets:
  N1: 元件1.A0, R1.wiper
  N2: 元件1.GND, IC1.0V, R1.leg1
  N3: 元件1.D9_PWM, IC1.In_2
  N4: 元件1.D10_PWM/SS, IC1.In_1
  N5: 元件1.D11_PWM/MOSI, IC1.Enable_1
  N6: 元件1.5V, IC1.+V, R1.leg2
  N7: IC1.Out_1_(_Controlled_by_Enable_1_), M1.pin_1
  N8: IC1.Out_2_(_Controlled_by_Enable_1_), M1.pin_2

notes:
  ＋
  －
  GND
  5V
  A0
  11
  10
  9
