# Fritzing sketch ch10_servo (saved by Fritzing 0.8.3b)
breadboards: 1

parts:
  元件1 = Arduino Uno (Rev3)
  J1 = Basic Servo

nets:
  GND: 元件1.GND, J1.gnd
  N1: 元件1.D9_PWM, J1.pulse
  5V: 元件1.5V, J1.vcc

notes:
  5V
  GND
