# Fritzing sketch ch10_stepper_L293D (saved by Fritzing 0.8.3b)
breadboards: 1

parts:
  元件1 = Arduino Uno (Rev3)
  MOTOR1 = Adafruit Gear-Reduced Stepper Motor (small)
  IC1 = L293D [package=THT]

nets:
  N1: 元件1.GND, IC1.0V
  N2: 元件1.D11_PWM/MOSI, IC1.In_2
  N3: 元件1.D12/MISO, IC1.In_1
  N4: 元件1.5V, IC1.Enable_1
  N5: MOTOR1.RED, IC1.+Vmotor
  N6: MOTOR1.YELLOW, IC1.Out_2_(_Controlled_by_Enable_1_)
  N7: MOTOR1.BLUE, IC1.Out_1_(_Controlled_by_Enable_1_)

notes:
  ＋
  －

custom parts:
  Adafruit Gear-Reduced Stepper Motor (small): Adafruit gear-reduction stepper motor (small)
