# Fritzing sketch ch10_stepper_ULN2003 (saved by Fritzing 0.8.3b)
breadboards: 1

parts:
  元件1 = Arduino Uno (Rev3)
  MOTOR1 = Adafruit Gear-Reduced Stepper Motor (small)
  IC1 = ULN2003A [package="DIP16 [THT]"]

nets:
  N1: 元件1.GND, IC1.0V
  N2: 元件1.D9_PWM, IC1.In_4
  N3: 元件1.D10_PWM/SS, IC1.In_3
  N4: 元件1.D11_PWM/MOSI, IC1.In_2
  N5: 元件1.D12/MISO, IC1.In_1
  N6: MOTOR1.RED, IC1.COM_-_Common
  N7: MOTOR1.ORANGE, IC1.Out_4
  N8: MOTOR1.YELLOW, IC1.Out_2
  N9: MOTOR1.PINK, IC1.Out_3
  N10: MOTOR1.BLUE, IC1.Out_1

notes:
  ＋
  －

custom parts:
  Adafruit Gear-Reduced Stepper Motor (small): Adafruit gear-reduction stepper motor (small)
