# Fritzing sketch ch12_ArduinoISP (saved by Fritzing 0.8.3b)
breadboards: 1

parts:
  U1 = atmega328 [package=dip]
  R1 = Resistor [tolerance=±5% resistance=10k package=THT]
  S1 = Pushbutton [package="[THT]"]
  XTAL1 = Crystal [frequency="16 Mhz" package=THT]
  C1 = Capacitor [package=cap-pth-small2]
  C2 = Capacitor [package=cap-pth-small2]
  R2 = Resistor [tolerance=±5% resistance=220 package=THT]
  LED1 = LED - 5mm [color="Red (633nm)" package="5 mm [THT]"]
  元件1 = Arduino Uno (Rev3)

nets:
  N1: U1.RESET, R1.Pin_0, S1.Pin_1, S1.Pin_2, 元件1.D10_PWM/SS
  VCC: U1.VCC, U1.AVCC, R1.Pin_1, 元件1.5V
  GND: U1.GND, S1.Pin_3, S1.Pin_4, C1.2, C2.1, LED1.cathode, 元件1.GND
  N2: U1.XLAT1, XTAL1.pin_1, C2.2
  N3: U1.XLAT2, XTAL1.pin_0, C1.1
  N4: U1.D9_(PWM), R2.Pin_0
  N5: U1.D11_(PWM), 元件1.ICSP_MOSI, 元件1.D11_PWM/MOSI
  N6: U1.D12, 元件1.ICSP_MISO, 元件1.D12/MISO
  N7: U1.D13, 元件1.ICSP_SCK, 元件1.D13/SCK
  N8: R2.Pin_1, LED1.anode

notes:
  220Ω
  18~22pF
  10kΩ
