# Fritzing sketch ch12_usb_to_ttl_serial (saved by Fritzing 0.8.3b)
breadboards: 1

parts:
  U1 = atmega328 [package=dip]
  R1 = Resistor [tolerance=±5% resistance=10k package=THT]
  S1 = Pushbutton [package="[THT]"]
  XTAL1 = Crystal [frequency="16 Mhz" package=THT]
  C1 = Capacitor [package=cap-pth-small2]
  C2 = Capacitor [package=cap-pth-small2]
  R2 = Resistor [tolerance=±5% resistance=220 package=THT]
  LED1 = LED - 5mm [color="Red (633nm)" package="5 mm [THT]"]
  FTDI1 = FTDI Friend

nets:
  N1: U1.RESET, R1.Pin_0, S1.Pin_1, S1.Pin_2
  N2: U1.D0_(RX), FTDI1.TX
  N3: U1.D1_(TX), FTDI1.RX
  VCC: U1.VCC, U1.AVCC, R1.Pin_1, FTDI1.VCC
  GND: U1.GND, S1.Pin_3, S1.Pin_4, C1.2, C2.1, LED1.cathode, FTDI1.GND
  N4: U1.XLAT1, XTAL1.pin_1, C2.2
  N5: U1.XLAT2, XTAL1.pin_0, C1.1
  N6: U1.D9_(PWM), R2.Pin_0
  N7: R2.Pin_1, LED1.anode

notes:
  220Ω
  18~22pF
  10kΩ
